# Fritzing sketch Arduino on a breadboard with a atmega328p and cp2102 (saved by Fritzing 0.9.2b)
breadboards: 1

parts:
  U1 = atmega328 [package=dip]
  U2 = TTL UART CP2102
  16MHZ = CRYSTAL [part_number=crystal package=hc49u-v]
  2x_22_pF = Capacitor [part_number="(code 22 or 220)" package=cap-pth-small2]
  22pF1 = Capacitor [package=cap-pth-small2]
  0_10_uF = Capacitor [part_number="(code 104)" package=cap-pth-small2]
  part = Resistor [tolerance=±5% resistance=10k part_number=resistor package=THT]

nets:
  N1: U1.D0_(RX), U1.D6_(PWM), U1.D11_(PWM), U2.GND, 2x_22_pF.1, 22pF1.2
  N2: U1.D1_(TX), U1.D7
  N3: U1.D2, 16MHZ.2, 22pF1.1
  N4: U1.D9_(PWM), 0_10_uF.2, part.Pin_0
  N5: U1.D10_(PWM), U1.A3
  N6: U1.A4, U2.+5V, part.Pin_1
  N7: U2.DTR, 0_10_uF.1
  N8: 16MHZ.1, 2x_22_pF.2

custom parts:
  TTL UART CP2102: 6Pin USB 2.0 to TTL UART Module Serial Converter CP2102 STC Replace Ft232 Module
